# Fritzing sketch Rodel_sketch (saved by Fritzing 0.9.3b)

parts:
  Part1 = Arduino Nano (Rev3.0)
  S1 = Round Pushbutton
  Q1 = Basic FET P-Channel [package="TO220 [THT]"]
  Q2 = Basic FET P-Channel [package="TO220 [THT]"]  # not connected
  Q3 = TRANSISTOR_NPN [package=to-92-ammo]  # not connected
  Q4 = TRANSISTOR_NPN [package=to-92-ammo]
  R1 = Resistor [tolerance=±5% resistance=220 package=THT]
  U1 = POT [package=pot_alpha_rv16af-20]
  LED1 = LEDs [package=led10mm]
  LED2 = LEDs [package=led10mm]  # not connected
  R2 = Resistor [tolerance=±5% resistance=10k package=THT]
  J1 = Power Jack [package=power_jack_combo]
  R4 = Resistor [tolerance=±5% resistance=10k package=THT]
  R3 = Resistor [tolerance=±5% resistance=10k package=THT]

nets:
  N1: Part1.GND, S1.leg0, Q4.E, U1.A, R3.Pin_1
  N2: Part1.D2, R1.Pin_0
  N3: Part1.D3, R4.Pin_0
  N4: Part1.5V, U1.E
  N5: Part1.A1, U1.S
  N6: S1.leg1, R1.Pin_1
  N7: Q1.gate, Q4.C, R2.Pin_1
  N8: Q1.drain, R2.Pin_0, J1.PWR
  N9: Q1.source, LED1.C
  N10: Q4.B, R4.Pin_1
  N11: LED1.A, J1.GND
